# Fritzing sketch A4988-microstepping-test (saved by Fritzing 0.9.3b)

parts:
  Arduino_UNO_R3 = Arduino Uno (Rev3) - ICSP
  12v = Power plug
  42BYGH = Stepper Motor - Bipolar
  C2 = Electrolytic Capacitor [capacitance=100μF voltage=35V package="0807 [SMD, electrolytic]"]
  A4988_driver = A4988 Stepper Motor Driver Carrier

nets:
  N1: Arduino_UNO_R3.D8, A4988_driver.MS3
  N2: Arduino_UNO_R3.D9_PWM, A4988_driver.MS2
  N3: Arduino_UNO_R3.D10_PWM/SS, A4988_driver.MS1
  N4: Arduino_UNO_R3.D11_PWM/MOSI, A4988_driver.Enable
  N5: Arduino_UNO_R3.D2, A4988_driver.DIR
  N6: Arduino_UNO_R3.D3_PWM, A4988_driver.STEP
  5V: Arduino_UNO_R3.5V, A4988_driver.VDD
  N7: Arduino_UNO_R3.GND, A4988_driver.GROUND#147
  N8: 12v.GND, C2.-, A4988_driver.GROUND#141
  N9: 12v.VCC, C2.+, A4988_driver.VMOT
  N10: 42BYGH.A, A4988_driver.OUT_2B
  N11: 42BYGH.C, A4988_driver.OUT_2A
  N12: 42BYGH.B, A4988_driver.OUT_1A
  N13: 42BYGH.D, A4988_driver.OUT_1B
  N14: A4988_driver.RESET, A4988_driver.SLEEP

notes:
  https://github.com/durcanm/Arduino/
