# Fritzing sketch RFID-RC522 (saved by Fritzing 0.9.3b)

parts:
  Part1 = Arduino Uno (Rev3) - ICSP
  Part2 = RFID-RC522-v2
  Pro_Micro1 = Pro Micro
  Part3 = RFID-RC522-v2

nets:
  N1: Part1.ICSP_MOSI, Part1.D11_PWM/MOSI, Part2.MOSI
  N2: Part1.D9_PWM, Part2.RST
  N3: Part1.D10_PWM/SS, Part2.SDA
  N4: Part1.D12/MISO, Part2.MISO
  N5: Part1.D13/SCK, Part2.SCK
  GND: Part1.GND, Part2.GND
  3V3: Part1.3V3, Part2.3.3V
  N6: Pro_Micro1.D10, Part3.SDA
  N7: Pro_Micro1.D16/MOSI, Part3.MOSI
  N8: Pro_Micro1.D14/MISO, Part3.MISO
  N9: Pro_Micro1.D15/SCLK, Part3.SCK
  VCC: Pro_Micro1.VCC, Part3.3.3V
  N10: Pro_Micro1.RST, Part3.RST
  GND_2: Pro_Micro1.GND, Part3.GND

custom parts:
  RFID-RC522-v2: A simple China made RFID-RC522 Reader; do check the pin labels, as this is a MFRC522 based clone.
  Pro Micro: The SparkFun Pro Micro is a complete USB-based microcontoller development system, in a very small footprint, capable of implementing many types of projects. All programming can be done via the USB port.
