# Fritzing sketch 28byj48-xy-axis (saved by Fritzing 0.9.3b)
breadboards: 1

parts:
  Part1 = Arduino Uno (Rev3) - ICSP
  Part2 = Thumb Joystick
  U1 = POT [package=pot_alpha_rv16af-20]
  MOTOR1 = 28BYJ-48 Stepper Motor
  ULN2003A_-_Stepper_Driver_Board1 = ULN2003A - Stepper Driver Board [package=board]
  ULN2003A_-_Stepper_Driver_Board2 = ULN2003A - Stepper Driver Board [package=board]
  MOTOR2 = 28BYJ-48 Stepper Motor

nets:
  N1: Part1.A1, Part2.VERT
  N2: Part1.A2, Part2.HORZ
  N3: Part1.A5/SCL, U1.S
  N4: Part1.D8, ULN2003A_-_Stepper_Driver_Board1.IN1
  N5: Part1.D9_PWM, ULN2003A_-_Stepper_Driver_Board1.IN2
  N6: Part1.D10_PWM/SS, ULN2003A_-_Stepper_Driver_Board1.IN3
  N7: Part1.D11_PWM/MOSI, ULN2003A_-_Stepper_Driver_Board1.IN4, ULN2003A_-_Stepper_Driver_Board1.IN5
  N8: Part1.D12/MISO, Part2.SEL
  N9: Part1.D2, ULN2003A_-_Stepper_Driver_Board2.IN1
  N10: Part1.D3_PWM, ULN2003A_-_Stepper_Driver_Board2.IN2
  N11: Part1.D4, ULN2003A_-_Stepper_Driver_Board2.IN3
  N12: Part1.D5_PWM, ULN2003A_-_Stepper_Driver_Board2.IN4
  VCC: Part1.5V, Part2.VCC, U1.E, ULN2003A_-_Stepper_Driver_Board1.VCC, ULN2003A_-_Stepper_Driver_Board2.VCC
  GND: Part1.GND, Part2.GND, U1.A, ULN2003A_-_Stepper_Driver_Board1.GND, ULN2003A_-_Stepper_Driver_Board2.GND
  N13: MOTOR1.BLUE, ULN2003A_-_Stepper_Driver_Board1.BLUE
  N14: MOTOR1.PINK, ULN2003A_-_Stepper_Driver_Board1.PINK
  N15: MOTOR1.RED, ULN2003A_-_Stepper_Driver_Board1.RED
  N16: MOTOR1.ORANGE, ULN2003A_-_Stepper_Driver_Board1.ORANGE
  N17: MOTOR1.YELLOW, ULN2003A_-_Stepper_Driver_Board1.YELLOW
  N18: ULN2003A_-_Stepper_Driver_Board2.BLUE, MOTOR2.BLUE
  N19: ULN2003A_-_Stepper_Driver_Board2.PINK, MOTOR2.PINK
  N20: ULN2003A_-_Stepper_Driver_Board2.YELLOW, MOTOR2.YELLOW
  N21: ULN2003A_-_Stepper_Driver_Board2.ORANGE, MOTOR2.ORANGE
  N22: ULN2003A_-_Stepper_Driver_Board2.RED, MOTOR2.RED

notes:
  1 Kohm
  2 axis joystick
  ULN2003a stepper motor driver
  28BYJ-48 stepper motor
  https://github.com/durcanm/Arduino/

custom parts:
  28BYJ-48 Stepper Motor: 28BYJ-48 gear-reduction stepper motor (small)
  ULN2003A - Stepper Driver Board: A common stepper motor driver board based on ULN2003APG darlington array
