# Fritzing sketch engraver-v1.1 (saved by Fritzing 0.9.3b)
breadboards: 2

parts:
  Arduino_Mega_2560 = Arduino Mega 2560 (Rev3)
  1K_pot = POT [package=pot_alpha_rv16af-20]
  XY_axis = Thumb Joystick
  Z_axis = Thumb Joystick
  10_000_rpm_DC = DC Motor
  L298_Driver = H-Bridge with L298N
  DC_motor_button = Round Pushbutton
  R1 = Resistor [tolerance=±5% resistance=10k package=THT]
  AutoDrive_button = Round Pushbutton
  R2 = Resistor [tolerance=±5% resistance=10k package=THT]
  LED2 = smd LED [color="Red (633nm)" package="0805 [SMD]"]
  R3 = Resistor [tolerance=±5% resistance=330 package="1206 [SMD]"]
  LED3 = smd LED [color="Green (565nm)" package="0805 [SMD]"]
  R4 = Resistor [tolerance=±5% resistance=330 package="1206 [SMD]"]
  A4988_driver = A4988 Stepper Motor Driver Carrier
  M6 = Stepper Motor - Bipolar
  12v = Power plug
  part = Electrolytic Capacitor [capacitance=100μF voltage=35V package="0807 [SMD, electrolytic]"]
  A4988_driver1 = A4988 Stepper Motor Driver Carrier
  part_2 = Electrolytic Capacitor [capacitance=100μF voltage=35V package="0807 [SMD, electrolytic]"]
  M7 = Stepper Motor - Bipolar
  A4988_driver3 = A4988 Stepper Motor Driver Carrier
  part_3 = Electrolytic Capacitor [capacitance=100μF voltage=35V package="0807 [SMD, electrolytic]"]
  M9 = Stepper Motor - Bipolar

nets:
  N1: Arduino_Mega_2560.A0, 1K_pot.S
  N2: Arduino_Mega_2560.A1, XY_axis.HORZ
  N3: Arduino_Mega_2560.A2, XY_axis.VERT
  N4: Arduino_Mega_2560.A3, Z_axis.VERT
  VCC: Arduino_Mega_2560.5V, 1K_pot.E, XY_axis.VCC, Z_axis.VCC, DC_motor_button.leg0, AutoDrive_button.leg0
  GND: Arduino_Mega_2560.GND, 1K_pot.A, XY_axis.GND, Z_axis.GND, R1.Pin_0, R2.Pin_0, R3.Pin_0, R4.Pin_0
  N5: Arduino_Mega_2560.D22, A4988_driver.Enable
  N6: Arduino_Mega_2560.D23, A4988_driver1.Enable
  N7: Arduino_Mega_2560.D24, A4988_driver.MS1
  N8: Arduino_Mega_2560.D25, A4988_driver1.MS1
  N9: Arduino_Mega_2560.D26, A4988_driver.STEP
  N10: Arduino_Mega_2560.D27, A4988_driver1.STEP
  N11: Arduino_Mega_2560.D28, A4988_driver.DIR
  N12: Arduino_Mega_2560.D29, A4988_driver1.DIR
  N13: Arduino_Mega_2560.D30, A4988_driver3.Enable
  N14: Arduino_Mega_2560.D32, A4988_driver3.MS1
  N15: Arduino_Mega_2560.D34, A4988_driver3.STEP
  N16: Arduino_Mega_2560.D36, A4988_driver3.DIR
  N17: Arduino_Mega_2560.D38, L298_Driver.ENA, L298_Driver.IN1
  N18: Arduino_Mega_2560.D40, L298_Driver.IN2, L298_Driver.IN3
  N19: Arduino_Mega_2560.D43, LED2.anode
  N20: Arduino_Mega_2560.D45, LED3.anode
  N21: Arduino_Mega_2560.D47, AutoDrive_button.leg1, R2.Pin_1
  N22: Arduino_Mega_2560.D49, DC_motor_button.leg1, R1.Pin_1
  N23: 10_000_rpm_DC.pin_1, L298_Driver.M1-02
  N24: 10_000_rpm_DC.pin_2, L298_Driver.M1-01
  12V: L298_Driver.12V, A4988_driver.VMOT, 12v.VCC, part.+, A4988_driver1.VMOT, part_2.+, A4988_driver3.VMOT, part_3.+
  GND_2: L298_Driver.GND, A4988_driver.GROUND#141, 12v.GND, part.-, A4988_driver1.GROUND, part_2.-, A4988_driver3.GROUND, part_3.-
  N25: LED2.cathode, R3.Pin_1
  N26: LED3.cathode, R4.Pin_1
  N27: A4988_driver.RESET, A4988_driver.SLEEP
  N28: A4988_driver.OUT_2B, M6.A
  N29: A4988_driver.OUT_2A, M6.C
  N30: A4988_driver.OUT_1A, M6.B
  N31: A4988_driver.OUT_1B, M6.D
  N32: A4988_driver1.RESET, A4988_driver1.SLEEP
  N33: A4988_driver1.OUT_2B, M7.A
  N34: A4988_driver1.OUT_2A, M7.C
  N35: A4988_driver1.OUT_1A, M7.B
  N36: A4988_driver1.OUT_1B, M7.D
  N37: A4988_driver3.RESET, A4988_driver3.SLEEP
  N38: A4988_driver3.OUT_2B, M9.A
  N39: A4988_driver3.OUT_2A, M9.C
  N40: A4988_driver3.OUT_1A, M9.B
  N41: A4988_driver3.OUT_1B, M9.D

notes:
  10K resistor
  Stepper LED
  AutoDrive LED
  https://github.com/durcanm/Arduino

custom parts:
  H-Bridge with L298N: h-bridge
