# Fritzing sketch engraver-v1.1a (saved by Fritzing 0.9.3b)

parts:
  Arduino_Mega_2560 = Arduino Mega 2560 (Rev3)
  1K_pot = POT [package=pot_alpha_rv16af-20]
  XY_axis = Thumb Joystick
  Z_axis = Thumb Joystick
  10_000_rpm_DC = DC Motor
  L298_Driver = H-Bridge with L298N
  DC_motor_button = Round Pushbutton
  R5 = Resistor [tolerance=±5% resistance=10k package=THT]
  AutoDrive_button = Round Pushbutton
  R6 = Resistor [tolerance=±5% resistance=10k package=THT]
  LED2 = smd LED [color="Red (633nm)" package="0805 [SMD]"]
  R3 = Resistor [tolerance=±5% resistance=330 package="1206 [SMD]"]
  LED3 = smd LED [color="Green (565nm)" package="0805 [SMD]"]
  R4 = Resistor [tolerance=±5% resistance=330 package="1206 [SMD]"]
  A4988_driver_#X = A4988 Stepper Motor Driver Carrier
  17HS3001-20B = Stepper Motor - Bipolar
  12v = Power plug
  C1 = Electrolytic Capacitor [capacitance=100μF voltage=35V package="0807 [SMD, electrolytic]"]
  A4988_driver_#Y = A4988 Stepper Motor Driver Carrier
  A4988_driver_#Z = A4988 Stepper Motor Driver Carrier
  12v_2 = Power plug

nets:
  N1: Arduino_Mega_2560.A0, 1K_pot.S
  N2: Arduino_Mega_2560.A1, XY_axis.VERT
  N3: Arduino_Mega_2560.A2, XY_axis.SEL, XY_axis.HORZ
  N4: Arduino_Mega_2560.A3, Z_axis.HORZ, Z_axis.VERT
  N5: Arduino_Mega_2560.D22, A4988_driver_#X.Enable
  N6: Arduino_Mega_2560.D24, A4988_driver_#X.MS1
  N7: Arduino_Mega_2560.D26, A4988_driver_#X.STEP
  N8: Arduino_Mega_2560.D28, A4988_driver_#X.DIR
  N9: Arduino_Mega_2560.D30, A4988_driver_#Y.Enable
  N10: Arduino_Mega_2560.D32, A4988_driver_#Y.MS1
  N11: Arduino_Mega_2560.D34, A4988_driver_#Y.STEP
  N12: Arduino_Mega_2560.D36, A4988_driver_#Y.DIR
  N13: Arduino_Mega_2560.D38, A4988_driver_#Z.Enable
  N14: Arduino_Mega_2560.D40, A4988_driver_#Z.MS1
  N15: Arduino_Mega_2560.D42, A4988_driver_#Z.STEP
  N16: Arduino_Mega_2560.D43, LED2.anode
  N17: Arduino_Mega_2560.D44, A4988_driver_#Z.DIR
  N18: Arduino_Mega_2560.D45, LED3.anode
  N19: Arduino_Mega_2560.D47, AutoDrive_button.leg1, R6.Pin_1
  N20: Arduino_Mega_2560.D49, DC_motor_button.leg1, R5.Pin_1
  N21: Arduino_Mega_2560.D50, L298_Driver.ENA, L298_Driver.IN1
  N22: Arduino_Mega_2560.D52, L298_Driver.IN2, L298_Driver.IN3, L298_Driver.IN4
  N23: 10_000_rpm_DC.pin_1, L298_Driver.M1-02
  N24: 10_000_rpm_DC.pin_2, L298_Driver.M1-01
  12V: L298_Driver.12V, 12v_2.VCC
  GND: L298_Driver.GND, 12v_2.GND
  N25: LED2.cathode, R3.Pin_1
  N26: LED3.cathode, R4.Pin_1
  N27: A4988_driver_#X.RESET, A4988_driver_#X.SLEEP
  N28: A4988_driver_#X.VMOT, 12v.VCC, C1.+
  N29: A4988_driver_#X.GROUND#141, 12v.GND, C1.-
  N30: A4988_driver_#X.OUT_2B, 17HS3001-20B.A
  N31: A4988_driver_#X.OUT_2A, 17HS3001-20B.C
  N32: A4988_driver_#X.OUT_1A, 17HS3001-20B.B
  N33: A4988_driver_#X.OUT_1B, 17HS3001-20B.D
  N34: A4988_driver_#Y.RESET, A4988_driver_#Y.SLEEP
  N35: A4988_driver_#Z.RESET, A4988_driver_#Z.SLEEP

notes:
  Stepper LED
  AutoDrive LED
  https://github.com/durcanm/Arduino

custom parts:
  H-Bridge with L298N: h-bridge
